# Fritzing sketch Schematic Form (saved by Fritzing 0.9.3b)
breadboards: 1

parts:
  Raspberry_Pi_1 = Raspberry Pi 3 [part_number=RPI-3-V1.2]
  LED1 = LED - 5mm [color="Red (633nm)" package="5 mm [THT]"]
  LED2 = LED - 5mm [color="Red (633nm)" package="5 mm [THT]"]
  LED3 = LED - 5mm [color="Red (633nm)" package="5 mm [THT]"]
  LED4 = LED - 5mm [color="Red (633nm)" package="5 mm [THT]"]
  LED5 = LED - 5mm [color="Red (633nm)" package="5 mm [THT]"]
  LED6 = LED - 5mm [color="Red (633nm)" package="5 mm [THT]"]
  LED7 = LED - 5mm [color="Red (633nm)" package="5 mm [THT]"]
  LED8 = LED - 5mm [color="Red (633nm)" package="5 mm [THT]"]
  R1 = Resistor [tolerance=±5% resistance=220 package=THT]
  R2 = Resistor [tolerance=±5% resistance=220 package=THT]
  R3 = Resistor [tolerance=±5% resistance=220 package=THT]
  R4 = Resistor [tolerance=±5% resistance=220 package=THT]
  R5 = Resistor [tolerance=±5% resistance=220 package=THT]
  R6 = Resistor [tolerance=±5% resistance=220 package=THT]
  R7 = Resistor [tolerance=±5% resistance=220 package=THT]
  R8 = Resistor [tolerance=±5% resistance=220 package=THT]

nets:
  N1: Raspberry_Pi_1.GPIO17, LED8.anode
  N2: Raspberry_Pi_1.GPIO27, LED7.anode
  N3: Raspberry_Pi_1.GPIO22, LED6.anode
  N4: Raspberry_Pi_1.GND, R1.Pin_1, R2.Pin_1, R3.Pin_1, R4.Pin_1, R5.Pin_1, R6.Pin_1, R7.Pin_1, R8.Pin_1
  N5: Raspberry_Pi_1.GPIO5, LED5.anode
  N6: Raspberry_Pi_1.GPIO6, LED4.anode
  N7: Raspberry_Pi_1.GPIO13, LED3.anode
  N8: Raspberry_Pi_1.GPIO19, LED2.anode
  N9: Raspberry_Pi_1.GPIO26, LED1.anode
  N10: LED1.cathode, R1.Pin_0
  N11: LED2.cathode, R2.Pin_0
  N12: LED3.cathode, R3.Pin_0
  N13: LED4.cathode, R4.Pin_0
  N14: LED5.cathode, R5.Pin_0
  N15: LED6.cathode, R6.Pin_0
  N16: LED7.cathode, R7.Pin_0
  N17: LED8.cathode, R8.Pin_0
